// Logisim project data_path.circ as structural Verilog: 1 circuit, main circuit main
module main (
  output [31:0] out_1,
  output [31:0] out_2,
  output [31:0] out_3,
  output [31:0] out_4,
  output [31:0] out_5,
  output [31:0] out_6,
  output [31:0] out_7,
  output [31:0] out_8,
  output [31:0] out_9,
  output [31:0] out_10,
  output [31:0] out_11,
  output [31:0] out_12,
  output [31:0] out_13,
  output [31:0] out_14,
  output [31:0] out_15,
  output [31:0] out_16,
  output [31:0] out_17,
  output [31:0] out_18,
  output [31:0] out_19,
  output [31:0] out_20,
  output [31:0] out_21,
  output [31:0] out_22,
  output [31:0] out_23,
  output [31:0] out_24,
  output [31:0] out_25,
  output [31:0] out_26,
  output [31:0] out_27,
  output [31:0] out_28,
  output [31:0] out_29,
  output [31:0] out_30,
  output [31:0] out_31,
  output [31:0] out_32,
  output [31:0] out_33,
  output out_34,
  output out_35
);

  wire clock, Extop, jalr, LessFlagSigned, LessFlagUnsigned, mem_to_reg, Memory_Write, MemRead, pc_src,
       RegWrite, SSET, ZeroFlag;
  wire [1:0] ALUsrc;
  wire [4:0] Imm16, ImmL, multiplexer_3_out;
  wire [7:0] ALU_Op;
  wire [10:0] Funct;
  wire [15:0] instruction;
  wire [19:0] pc, pc_inc, pc_next;
  wire [31:0] ALU_Result, bit_extender_1_out, bit_extender_2_out, bit_extender_3_out, bit_extender_4_out,
       BusA, BusB, main_1_p6, multiplexer_1_out, multiplexer_4_out, multiplexer_5_out, Write_Data;

  // Probe on ALU_Result
  // data_mem_main main_1: pin names not known; wires that end beside it: ALU_Result, BusB, clock, MemRead, Memory_Write, main_1_p6
  // Probe on main_1_p6
  Clock clock_1 (.out(clock));
  // Probe on ALU_Result
  // Probe on instruction[5:0]
  // pc_circut_main main_2: pin names not known; wires that end beside it: {Funct, Imm16}, Funct, ImmL, BusA, clock, pc_src, jalr, pc_next, pc_inc, pc
  Multiplexer #(.width(32), .enable("false")) multiplexer_1 (
    .in0(ALU_Result), .in1(main_1_p6), .out(multiplexer_1_out), .sel(mem_to_reg));
  assign bit_extender_1_out = {{12{1'b0}}, pc_inc};  // Bit_Extender bit_extender_1
  // Probe on pc_next
  Multiplexer #(.width(32), .enable("false")) multiplexer_2 (
    .in0(multiplexer_1_out), .in1(bit_extender_1_out), .out(Write_Data), .sel(jalr));
  // Probe on pc
  ROM #(.addrWidth(20), .dataWidth(32)) rom_1 (
    .addr(pc), .data({Funct, Imm16, instruction[15:11], ImmL, instruction[5:0]}));
  // Probe on pc_inc
  // Probe on pc
  // Probe on instruction[15:11]
  // Probe on instruction[5:0]
  // Probe on instruction[15:11]
  // Probe on ImmL
  // Probe on {Funct, Imm16}
  // Probe on ImmL
  // Probe on Funct
  // Probe on {Funct, Imm16, instruction[15:11], ImmL, instruction[5:0]}
  MainControlUnit_main main_3 (
    .ALU_Op(ALU_Op), .mem_to_reg(mem_to_reg), .Memory_Read(MemRead), .Memory_Write(Memory_Write),
    .RegWrite(RegWrite), .in_1(Funct), .Extop(Extop), .ALUsrc(ALUsrc), .in_2(instruction[5:0]), .SSET(SSET),
    .jalr(jalr), .Pc_src(pc_src), .ZeroFlag(ZeroFlag), .LessFlagSigned(LessFlagSigned),
    .LessFlagUnsigned(LessFlagUnsigned));
  Multiplexer #(.width(5), .enable("false")) multiplexer_3 (
    .in0(instruction[15:11]), .in1(ImmL), .out(multiplexer_3_out), .sel(SSET));
  assign bit_extender_2_out = {{16{1'b0}}, {Funct, Imm16}};  // Bit_Extender bit_extender_2
  assign bit_extender_3_out = {{16{Funct[10]}}, {Funct, Imm16}};  // Bit_Extender bit_extender_3
  assign bit_extender_4_out = {{16{Funct[10]}}, {Funct, ImmL}};  // Bit_Extender bit_extender_4
  // Probe on ImmL
  Multiplexer #(.width(32), .enable("false")) multiplexer_4 (
    .in0(bit_extender_2_out), .in1(bit_extender_3_out), .out(multiplexer_4_out), .sel(Extop));
  // Probe on Write_Data
  Multiplexer #(.select(2), .width(32), .enable("false")) multiplexer_5 (
    .in0(BusB), .in1(multiplexer_4_out), .in2(bit_extender_4_out), .out(multiplexer_5_out), .sel(ALUsrc));  // open: in3
  // ALU_Full alu_full_1: pin names not known; wires that end beside it: BusA, multiplexer_5_out, ALU_Op[5:4], ALU_Op[7], ALU_Op[6], ALU_Op[6], ALU_Op[3:0], ALU_Result, LessFlagUnsigned, LessFlagSigned, out_34, out_35, ZeroFlag
  // Reg_file reg_file_1: pin names not known; wires that end beside it: multiplexer_3_out, Imm16, ImmL, clock, out_1, out_2, out_4, out_6, out_9, RegWrite, out_11, out_13, out_15, out_17, out_19, out_21, out_23, Write_Data, out_25, out_27, out_29, out_31, out_33, out_3, out_5, out_7, out_10, out_12, out_14, out_16, out_18, out_20, out_22, out_24, out_26, out_28, out_30, out_32, BusA, BusB
  // Probe on ALU_Result
  // Probe on BusB

  assign out_8 = out_7;

  // Other names for the same wires on the sheet: OP[5:0] = instruction[5:0];
  //   instruction (some bits) = {Funct, Imm16, ImmL}; Rd[4:0] = ImmL; Rs1[4:0] = instruction[15:11]; Rs2[4:0] = Imm16;
  //   Imm16[15:5] = Funct; ImmU[10:0] = Funct; R0[31:0] = out_1; R1[31:0] = out_2; R2[31:0] = out_4; R3[31:0] = out_6;
  //   R4[31:0] = out_9; R5[31:0] = out_11; R6[31:0] = out_13; R7[31:0] = out_15; R8[31:0] = out_17; R9[31:0] = out_19;
  //   R10[31:0] = out_21; R11[31:0] = out_23; R12[31:0] = out_25; R13[31:0] = out_27; R14[31:0] = out_29;
  //   R15[31:0] = out_31; R16[31:0] = out_33; R17[31:0] = out_3; R18[31:0] = out_5; R19[31:0] = out_7;
  //   R20[31:0] = out_10; R21[31:0] = out_12; R22[31:0] = out_14; R23[31:0] = out_16; R24[31:0] = out_18;
  //   R25[31:0] = out_20; R26[31:0] = out_22; R27[31:0] = out_24; R28[31:0] = out_26; R29[31:0] = out_28;
  //   R30[31:0] = out_30; R31[31:0] = out_32

  // Notes on the sheet:
  //   Registers
  //   Data_Memory
  //   contents of rom_1 (hex, n*v repeats v):
  //   0 1000004d 2000004e 5008d 300cd 831100 a32140 1252180 14231c0 1653a00 1831240 1a31280 10652c0 c21b00
  //   e21b40 21b80 2273c0 427400 627440 28c81 194c2 19503 49544 64ad85 c8b5c6 c8b607 1be48 ffce89 fd6ca
  //   f0df0b aae74c ffff078d ff07ce 40811 a10 50911 40a50 44092 6f0285 de0285 54893 14d02c5 1bc02c5 21894
  //   370305 420305 21895 4d0345 580345 21896 630385 640385 21897 6f03c5 de03c5 4104f 820900 a11940
  //   1630980 14311c0 1220a00 c20a40 1021280 14311c0 1220a00 c20a40 1021280
  //   Instruction_Memory
  //   Decoding_Instruction
  //   signal
  //   old_Rd_for_sset_instruction
  //   ALU
endmodule
